# Fritzing sketch esquema_Pulsador2-Led (saved by Fritzing 0.9.3b)

parts:
  Raspberry_Pi_1 = Raspberry Pi 3 [part_number=RPI-3-V1.2]
  S1 = Round Pushbutton
  LED1 = smd LED [color="Red (633nm)" package="1206 [SMD]"]

nets:
  N1: Raspberry_Pi_1.GPIO4, S1.leg0
  N2: Raspberry_Pi_1.GND, S1.leg1, LED1.cathode
  N3: Raspberry_Pi_1.GPIO21, LED1.anode
