# Fritzing sketch esquema_LedBlink (saved by Fritzing 0.9.3b)
breadboards: 1

parts:
  Raspberry_Pi_1 = Raspberry Pi 3 [part_number=RPI-3-V1.2]
  LED1 = LEDs [package=led10mm]
  R1 = Resistor [tolerance=±5% resistance=1k package="0402 [SMD]"]

nets:
  N1: Raspberry_Pi_1.GPIO17, LED1.A
  N2: Raspberry_Pi_1.GND, R1.Pin_1
  N3: LED1.C, R1.Pin_0
