# Fritzing sketch esquema_Pulsador0 (saved by Fritzing 0.9.3b)

parts:
  Raspberry_Pi_1 = Raspberry Pi 3 [part_number=RPI-3-V1.2]
  S1 = Round Pushbutton

nets:
  N1: Raspberry_Pi_1.GPIO4, S1.leg0
  N2: Raspberry_Pi_1.GND, S1.leg1
